# Fritzing sketch logger (saved by Fritzing 0.9.2b)
circuit board: 10cm x 6cm

parts:
  Raspberry_Pi_1 = Raspberry Pi 3 [part_number=RPI-3-V1.2]
  LCD1 = LCD screen
  Part1 = Adafruit MAX31856 Thermocouple Amp [part_number="Adafruit #3263"]

nets:
  3V3: Raspberry_Pi_1.3V3, Part1.3.3V
  N1: Raspberry_Pi_1.GIPO10, Part1.SDI
  N2: Raspberry_Pi_1.GIPO9, Part1.SDO
  N3: Raspberry_Pi_1.GIPO11, Part1.SCK
  N4: Raspberry_Pi_1.GIPO8, Part1.!FAULT, Part1.!CS
  GND: Raspberry_Pi_1.GND, Part1.GND
  N5: LCD1.VSS, LCD1.R/W, LCD1.LED-

notes:
  GRND
  Vcc
  SDA
  SCL

custom parts:
  Adafruit MAX31856 Thermocouple Amp: Thermocouples are very sensitive, requiring a good amplifier with a cold-compensation reference, as well as calculations to handle any non-linearities. For a long time we've suggested our MAX31855K breakout, which works great but is only for K-type thermocouples. Now we're happy to offer a great new thermocouple amplifier/converter that can handle just about any type of thermocouple, and even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
